# Fritzing sketch esp2866_breakout (saved by Fritzing 0.9.3b)
circuit board: 2cm x 3cm
breadboards: 1

parts:
  U2 = 555 Timer [package="DIP8 [THT]"]
  U1 = ESP8266 WiFi Module [part_number=ESP8266]

nets:
  N1: U2.Ground, U1.RXD
  N2: U2.Trigger, U1.VCC
  N3: U2.Output, U1.GPIO_0
  N4: U2.Reset, U1.RST
  N5: U2.Control_Voltage, U1.GPIO_2
  N6: U2.Threshold, U1.CH_PD
  N7: U2.Discharge, U1.GND
  N8: U2.Vcc_Supply_Voltage, U1.TXD

notes:
  8266-01 breakout
  heeed0002

custom parts:
  ESP8266 WiFi Module: Generic WiFi Module based on the ESP8266 with onboard PCB antenna and UART communications
